# Fritzing sketch Sketch (saved by Fritzing 1.0.1rc)
breadboards: 1

parts:
  <-To_Door_Control = 1 chan 5v relay module
  2A_DC_Boost_5V->12V = MT3608 Module
  <-To_Door_Sensor = Screw terminal - 2 pins [package=THT]
  C1 = Electrolytic Capacitor [capacitance=0.47mF voltage=16V package="300 mil [THT, electrolytic]"]
  5V_DC_In = Screw terminal - 2 pins [package=THT]
  3_3->5V = Logic Level Converter
  12V_DC_Case_Fan = DC Motor [voltage_(max)=12V voltage_(min)=12V]
  5V_Neopixel_LED_Strip = Neopixel Strip -- Black (30/m) [part_number=1376]
  TFmini-S_Header = Header 4 [package=screwterminal-3.5mm-4_lock]
  TFmini-S = Header 4 [package=screwterminal-3.5mm-4_lock]
  MCU1 = Raspberry Pi Zero 2W

nets (from the breadboard view):
  N1: <-To_Door_Control.pin_1, 2A_DC_Boost_5V->12V.pin2, C1.+, 5V_DC_In.pin1, 3_3->5V.HV, 5V_Neopixel_LED_Strip.+5V, TFmini-S_Header.3, TFmini-S.2, MCU1.pin_2, MCU1.pin_4
  GND: <-To_Door_Control.pin_2, 2A_DC_Boost_5V->12V.pin1, <-To_Door_Sensor.pin1, C1.-, 5V_DC_In.pin2, 3_3->5V.GND, 5V_Neopixel_LED_Strip.GND, TFmini-S_Header.4, MCU1.pin_6, MCU1.pin_25, MCU1.pin_34, MCU1.pin_39
  N2: <-To_Door_Control.pin_3, MCU1.pin_11
  N3: 2A_DC_Boost_5V->12V.pin3, 12V_DC_Case_Fan.pin_2
  N4: 2A_DC_Boost_5V->12V.pin4, 12V_DC_Case_Fan.pin_1
  N5: <-To_Door_Sensor.pin2, MCU1.pin_3
  N6: 3_3->5V.LV, MCU1.pin_1, MCU1.pin_17
  N7: 3_3->5V.TX_LV, MCU1.pin_40
  N8: 3_3->5V.TX_HV, 5V_Neopixel_LED_Strip.Din
  N9: TFmini-S_Header.1, TFmini-S.4, MCU1.pin_10
  N10: TFmini-S_Header.2, TFmini-S.3, MCU1.pin_8

custom parts:
  1 chan 5v relay module: 1 Channel 5V Relay Module Board Shield with Optocoupler Support High and Low Level Trigger for Arduino.
  MT3608 Module: MT3608 Boost Converter Module Links: Aerosemi MT3608 2A Step Up Converter datasheet
  Neopixel Strip -- Black (30/m): These NeoPixel strips have 30 digitally-addressable pixel LEDs per meter and are very affordable and are only 12.5 mm wide, 10 mm if you remove the strip from the casing.
  Raspberry Pi Zero 2W: The Raspberry Pi Zero is half the size of a Model A+, with twice the utility. A tiny Raspberry Pi that’s affordable enough for any project! · 1Ghz, Single-core CPU · 512MB RAM · Mini HDMI and USB On-The-Go ports · Micro USB power · HAT-compatible 40-pin header. Jan 2018: In this version schematic has been changed so the pins match the GPIO connector. I.e. the left hand pins are all the pins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
